# Fritzing sketch esquema (saved by Fritzing 0.9.3b)

parts:
  U2 = ESP8266 NodeMCU LoLin module
  LED1 = LED - 5mm [color="Red (633nm)" package="5 mm [THT]"]
  LED2 = LED - 5mm [color="Green (555nm)" package="5 mm [THT]"]
  Componente1 = RFID-RC522-v2
  R1 = Resistor [tolerance=±5% resistance=220 package=THT]

nets:
  N1: U2.D1, Componente1.RST
  N2: U2.D2, Componente1.SDA
  3V3: U2.3V3, LED1.anode, Componente1.3.3V
  GND: U2.GND, LED2.cathode, Componente1.GND
  N3: U2.D5, Componente1.SCK
  N4: U2.D6, Componente1.MISO
  N5: U2.D7, Componente1.MOSI
  N6: U2.S3, R1.Pin_1
  N7: LED1.cathode, LED2.anode

custom parts:
  ESP8266 NodeMCU LoLin module: ESP8266 based NodeMCU
  RFID-RC522-v2: A simple China made RFID-RC522 Reader; do check the pin labels, as this is a MFRC522 based clone.
